// Logisim project 74245.circ as structural Verilog: 1 circuit, main circuit 27245
module _27245 (
  input  DIR,
  input  ENABLE,
  input  A0,
  input  A1,
  input  A2,
  input  A3,
  input  A4,
  input  A5,
  input  A6,
  input  A7,
  output B0,
  output B1,
  output B2,
  output B3,
  output B4,
  output B5,
  output B6,
  output B7
);

  wire and_1_out, and_2_out, not_1_out, not_2_out, not_3_out;

  not not_1 (not_1_out, ENABLE);
  and and_1 (and_1_out, DIR, not_1_out);
  assign B0 = and_1_out ? A0 : 1'bz;  // Controlled_Buffer controlled_buffer_1
  assign B1 = and_1_out ? A1 : 1'bz;  // Controlled_Buffer controlled_buffer_2
  assign B2 = and_1_out ? A2 : 1'bz;  // Controlled_Buffer controlled_buffer_3
  assign B3 = and_1_out ? A3 : 1'bz;  // Controlled_Buffer controlled_buffer_4
  assign B4 = and_1_out ? A4 : 1'bz;  // Controlled_Buffer controlled_buffer_5
  assign B5 = and_1_out ? A5 : 1'bz;  // Controlled_Buffer controlled_buffer_6
  assign B6 = and_1_out ? A6 : 1'bz;  // Controlled_Buffer controlled_buffer_7
  assign B7 = and_1_out ? A7 : 1'bz;  // Controlled_Buffer controlled_buffer_8
  not not_2 (not_2_out, DIR);
  and and_2 (and_2_out, not_2_out, not_3_out);
  not not_3 (not_3_out, ENABLE);
  assign A0 = and_2_out ? B0 : 1'bz;  // Controlled_Buffer controlled_buffer_9
  assign A1 = and_2_out ? B1 : 1'bz;  // Controlled_Buffer controlled_buffer_10
  assign A2 = and_2_out ? B2 : 1'bz;  // Controlled_Buffer controlled_buffer_11
  assign A3 = and_2_out ? B3 : 1'bz;  // Controlled_Buffer controlled_buffer_12
  assign A4 = and_2_out ? B4 : 1'bz;  // Controlled_Buffer controlled_buffer_13
  assign A5 = and_2_out ? B5 : 1'bz;  // Controlled_Buffer controlled_buffer_14
  assign A6 = and_2_out ? B6 : 1'bz;  // Controlled_Buffer controlled_buffer_15
  assign A7 = and_2_out ? B7 : 1'bz;  // Controlled_Buffer controlled_buffer_16
endmodule
